# Fritzing sketch SoftAirBomb (saved by Fritzing 0.9.4)
circuit board: 8.46667cm x 5.64444cm

parts:
  Arduino = Arduino Uno (Rev3) - ICSP
  Buzzer = Piezo Speaker
  Alarm_Relay = RELAY [package=relay-jzc]
  Extra_Relay = RELAY [package=relay-jzc]
  Green = LED - 5mm [color="Green (555nm)" package="5 mm [THT]"]
  Red = LED - 5mm [color="Red (633nm)" package="5 mm [THT]"]
  Blue = LED - 5mm [color="Blue (430nm)" package="5 mm [THT]"]
  Boom = LED - 5mm [color="Yellow (595nm)" package="5 mm [THT]"]
  LCD_4x20 = Grove OLED 128x96
  KeyPad_4x4 = Camdenboss CTB0158-8 [part_number=CTB0158-8 package=THT]
  Red_Squad = Round Pushbutton
  SmartCard = SWITCH-MOMENTARY-2 [package=tactile-switch-1101ne]
  Green_Squad = Round Pushbutton

nets:
  N1: Arduino.A0, KeyPad_4x4.terminal_1
  N2: Arduino.A1, KeyPad_4x4.terminal_2
  N3: Arduino.A2, KeyPad_4x4.terminal_3
  N4: Arduino.A3, KeyPad_4x4.terminal_4, Red_Squad.leg1, Green_Squad.leg1
  N5: Arduino.ICSP_MISO, Arduino.D12/MISO, Blue.anode
  5V: Arduino.5V, Alarm_Relay.NC, Extra_Relay.NC, LCD_4x20.VCC
  N6: Arduino.ICSP_SCK, Arduino.D13/SCK, Buzzer.pin2
  N7: Arduino.ICSP_MOSI, Arduino.D11_PWM/MOSI, Red.anode
  GND: Arduino.GND, Buzzer.pin1, Alarm_Relay.COIL2, Extra_Relay.COIL2, Green.cathode, Red.cathode, Blue.cathode, Boom.cathode, LCD_4x20.GND, SmartCard.1
  N8: Arduino.D8, Extra_Relay.NO
  N9: Arduino.D9_PWM, Alarm_Relay.NO
  N10: Arduino.D10_PWM/SS, Green.anode
  N11: Arduino.D0/RX, KeyPad_4x4.terminal_5
  N12: Arduino.D1/TX, KeyPad_4x4.terminal_6
  N13: Arduino.D2, KeyPad_4x4.terminal_7, Green_Squad.leg0
  N14: Arduino.D3_PWM, KeyPad_4x4.terminal_8, Red_Squad.leg0
  N15: Arduino.D4, LCD_4x20.SDA
  N16: Arduino.D5_PWM, LCD_4x20.SCL
  N17: Arduino.D6_PWM, Boom.anode
  N18: Arduino.D7, SmartCard.2

// code stored in the sketch: SoftAirBomb.ino
#include <Wire.h>
#include <EEPROMex.h>
#include <Keypad.h>
//#include "I2CIO.h"
//#include "LCD.h"
#include <LiquidCrystal_I2C.h>
#include <avr/wdt.h>

// CONFIG TYPE
#define CONFIG_VERSION "GB5"

// EEPROM
#define memoryBase 32
int configAdress=0;
struct ConfigStruct {
    char version[4];
    int GH, GM, GB, GA, GS, GC, GP, SQ;          
    int T1, T2, TA, TE, TB;
};
ConfigStruct ConfigData;
ConfigStruct TestData;

// LCD
LiquidCrystal_I2C lcd(0x27, 20, 4); // CONNESSO A4=SDA A5=SCL     LCD 20x4

// KEYPAD
const byte ROWS = 4;
const byte COLS = 4;
char keys[ROWS][COLS] = { { '1', '2', '3', 'a' } , { '4', '5', '6', 'b' } , { '7', '8', '9', 'c' } , { '*', '0', '#', 'd' } };
byte rowPins[ROWS] = {  0, 1, 2, 3 };         // CONNESSO D2-D5
byte colPins[COLS] = {  A3, A2, A1, A0 };     // CONNESSO A3-A0
Keypad KeyPad = Keypad( makeKeymap(keys), rowPins, colPins, ROWS, COLS );

// SMARTCARD
const int SMARTCARD = 7;        // CONNESSO D7

// LEDS
const int BTNLED   = 12;        // CONNESSO D12
const int REDLED   = 11;        // CONNESSO D11
const int GREENLED = 10;        // CONNESSO D10
const int BOOMLED  =  6;        // CONNESSO D6

// ALARM RELAYS
const int ALARM = 9;            // CONNESSO D9

// SECOND RELAYS
const int RELAY = 8;            // CONNESSO D8

// TONE
int TonePin = 13;               // CONNESSO D13
int ToneAlarm1 = 700;
int ToneAlarm2 = 2600;
int ToneArming = 1330;
int ToneError = 100;
int ToneBip = 2400;

// TIME GAME e OPTIONS
short int GAMEHOURS = 0;
short int GAMEMINUTES = 45;
short int BOMBMINUTES = 5;
short int ACTIVATESECONDS = 15;
short int CAPTURESECONDS = 20;
short int CATCHPOINTMINUTES = 3;
short int SQLIFES = 15;
byte time[4];
bool ALARMACTIVE = true;
bool SMARTCARDACTIVE = false;
bool PASSWORDACTIVE = false;
char enteredText[4];
char password[4];
char temptext[4];
bool PLAYING = false;
long iTime;
short int minutos;

// VARIABLES
bool DEFUSE = false;
bool ARMING = false;
short int GAMETYPE = 0;

void setup() {
  lcd.begin(20,4);
  lcd.backlight();
  KeyPad.setHoldTime(50);
  KeyPad.setDebounceTime(50);
  KeyPad.addEventListener(KeyPadEvent);
  pinMode(GREENLED, OUTPUT);
  pinMode(REDLED, OUTPUT);
  pinMode(BTNLED, OUTPUT);
  pinMode(ALARM, OUTPUT);
  pinMode(RELAY, OUTPUT);
  pinMode(SMARTCARD, INPUT);
  digitalWrite(ALARM, LOW);
  digitalWrite(RELAY, LOW);
  tone(TonePin, ToneBip, 90);
  LCD_Welcome();
  LCD_CreateBar();
  EEPROM.setMemPool(memoryBase, EEPROMSizeUno);
  configAdress  = EEPROM.getAddress(sizeof(ConfigStruct)); 
  if(CheckConfig()){LoadConfig();}
  LCD_Cls();
}

void loop(){
  MenuMain();
}

void Capture() {
  StartGameCount();
  LCD_Cls();
  digitalWrite(REDLED, LOW);
  digitalWrite(GREENLED, LOW);
  lcd.setCursor(0, 2);
  lcd.print("--------------------");
  lcd.setCursor(0, 3);
  lcd.print("CATTURA LA BANDIERA ");
  minutos = GAMEMINUTES - 1;
  iTime=0;
  PLAYING = false;
  PlayForCapture();
}

void PlayForCapture() {
  unsigned long timeCalcVar;
  unsigned long aTime;
  if (PLAYING = true) {
    iTime = millis();
  }
  while (1) {
    timeCalcVar = (millis() - iTime) % 1000;
    if (timeCalcVar >= 0 && timeCalcVar <= 50)
    {
      digitalWrite(GREENLED, HIGH);
    }
    if (timeCalcVar >= 90 && timeCalcVar <= 130)
    {
      digitalWrite(GREENLED, LOW);
    }
    lcd.setCursor(0, 0);
    lcd.print("   TEMPO DI GIOCO   ");
    aTime = millis() - iTime;
    lcd.setCursor(5, 1);
    PrintTime(minutos, aTime);
    if (minutos - aTime / 60000 == 0 && 59 - ((aTime / 1000) % 60) == 0)
    {
      EndDefenderWin();
    }
    if (KeyPad.getKey() == 'd' && PASSWORDACTIVE == true && SMARTCARDACTIVE == false) {
      bool armings = ArmPassword("- - - CATTURA - - -");
      if (armings == true) {
        EndAttackerWin();
      }else{ALARM_OFF();}
    }
    if (digitalRead(SMARTCARD) == HIGH && SMARTCARDACTIVE == true) {
      bool armings = ArmSmartCard("- - - CATTURA - - -");
      if (armings == true) {
        EndAttackerWin();
      }else{ALARM_OFF();}
    }
    if (ARMING == true && PASSWORDACTIVE == false && SMARTCARDACTIVE == false) {
      bool armings = ArmKeyHold("- - - CATTURA - - -");
      if (armings == true) {
        EndAttackerWin();
      }else{ALARM_OFF();}
    }
  }
}

void Chrono(){
  StartGameCount();
  LCD_Cls();
  digitalWrite(11, LOW);
  digitalWrite(10, LOW);
  lcd.setCursor(0, 2);
  lcd.print("--------------------");
  lcd.setCursor(0, 3);
  lcd.print("       CHRONO       ");
  minutos = GAMEMINUTES - 1;
  iTime=0;
  PLAYING = false;
  PlayForChrono();
}

void PlayForChrono(){
  unsigned long timeCalcVar;
  unsigned long aTime;
  if(PLAYING = true){
    iTime = millis();
  }
  while (1) {
    timeCalcVar = (millis() - iTime) % 1000;
    if (timeCalcVar >= 0 && timeCalcVar <= 50)
    {
      digitalWrite(GREENLED, HIGH);
    }
    if (timeCalcVar >= 90 && timeCalcVar <= 130)
    {
      digitalWrite(GREENLED, LOW);
    }
    lcd.setCursor(0, 0);
    lcd.print("   TEMPO DI GIOCO   ");
    aTime = millis() - iTime;
    lcd.setCursor(5, 1);
    PrintTime(minutos, aTime);
    if (minutos - aTime / 60000 == 0 && 59 - ((aTime / 1000) % 60) == 0)
    {
      EndNoWin();
    }
  }
}

void Domination(){
  StartGameCount();
  LCD_Cls();
  digitalWrite(11, LOW);
  digitalWrite(10, LOW);
  lcd.setCursor(0, 2);
  lcd.print("--------------------");
  lcd.setCursor(0, 3);
  lcd.print("     DOMINAZIONE    ");
  minutos = GAMEMINUTES - 1;
  iTime=0;
  PLAYING = false;
  PlayForDom();
}

void PlayForDom(){
  unsigned long timeCalcVar;
  unsigned long aTime;
  if(PLAYING = true){
    iTime = millis();
  }
  lcd.setCursor(0, 0);
  lcd.print(" code under develop ");
  delay(3000);
  PlayAgain();
}

bool CheckConfig() {
  EEPROM.readBlock(configAdress, TestData);
  return (TestData.version == CONFIG_VERSION);
}

void LoadConfig() {
  EEPROM.readBlock(configAdress, ConfigData);
  GAMEHOURS = ConfigData.GH;
  GAMEMINUTES = ConfigData.GM;
  BOMBMINUTES = ConfigData.GB;
  ACTIVATESECONDS = ConfigData.GA;
  CAPTURESECONDS = ConfigData.GC;
  CATCHPOINTMINUTES = ConfigData.GP;
  SQLIFES = ConfigData.SQ;
  ToneAlarm1 = ConfigData.T1;
  ToneAlarm2 = ConfigData.T2;
  ToneArming = ConfigData.TA;
  ToneError = ConfigData.TE;
  ToneBip = ConfigData.TB;
}

void SaveConfig() {
  EEPROM.writeBlock(configAdress, ConfigData);
}

void SetConfig() {
  ConfigData = (ConfigStruct) {
    CONFIG_VERSION,
    GAMEHOURS, GAMEMINUTES, ACTIVATESECONDS, CAPTURESECONDS, CATCHPOINTMINUTES, SQLIFES,
    ToneAlarm1, ToneAlarm2, ToneArming, ToneError, ToneBip
  };
}

void Help(){
  tone(13, 2400, 30);
  LCD_Cls();
  switch (GAMETYPE) {
        case 0:
          lcd.setCursor(0, 0);
          lcd.print(F("Sq. A: Armare Bomba "));
          lcd.setCursor(0, 1);
          lcd.print(F("Sq. B: Sterminare A "));
          lcd.setCursor(0, 2);
          lcd.print(F("       o Disarmare  "));
          break;
        case 1:
          lcd.setCursor(0, 0);
          lcd.print(F("Sq. A: Armare Bomba "));
          lcd.setCursor(0, 1);
          lcd.print(F("Sq. B: Disarmare    "));
          lcd.setCursor(0, 2);
          lcd.print(F("Vince B per Tempo   "));
          break;
        case 2:
          lcd.setCursor(0, 0);
          lcd.print(F("Vince la Sq. che    "));
          lcd.setCursor(0, 1);
          lcd.print(F("mantiene il possesso"));
          lcd.setCursor(0, 2);
          lcd.print(F("per più tempo       "));
          break;
        case 3:
          lcd.setCursor(0, 0);
          lcd.print(F("Sq. A: Proteggere   "));
          lcd.setCursor(0, 1);
          lcd.print(F("Sq. B: Conquistare  "));
          lcd.setCursor(0, 2);
          lcd.print(F("Vince A per Tempo   "));
          break;
        case 4:
          lcd.setCursor(0, 0);
          lcd.print(F("Gestisce il Tempo   "));
          lcd.setCursor(0, 1);
          lcd.print(F("dei Rentri per Morte"));
          lcd.setCursor(0, 2);
          lcd.print(F("delle due squadre   "));
          break;
        case 5:
          lcd.setCursor(0, 0);
          lcd.print(F("Configurazioni      "));
          lcd.setCursor(0, 1);
          lcd.print(F("Globali e Test di   "));
          lcd.setCursor(0, 2);
          lcd.print(F("Funzionamento       "));
          break;
      }
  lcd.setCursor(0, 3);
  lcd.print(F("   Premi un tasto   "));
  PressAKey();
}

void KeyPadEvent(KeypadEvent key) {
  switch (KeyPad.getState()) {
    case PRESSED:
      break;
    case RELEASED:
      switch (key) {
        case 'd': DEFUSE = false;
          break;
        case 'c': ARMING = false;
          break;
      }
      break;
    case HOLD:
      switch (key) {
        case 'd': DEFUSE = true;
          break;
        case 'c': ARMING = true;
          break;
      }
      break;
  }
}

void PressKeyToStop() {
  lcd.setCursor(0, 1);
  lcd.print("Premi un tasto");
  KeyPad.waitForKey();
}

void PressAKey() {
  KeyPad.waitForKey();
}

bool KeyConfirm() {
  lcd.setCursor(13, 1);
  lcd.print("OK?");
  while (1) {
    char key = KeyPad.waitForKey();
    tone(TonePin, ToneBip, 30);
    if (key == 'c') {
      return false;
    }
    if (key == 'd') {
      return true;
    }
  }
}

bool KeyYesNo() {
  lcd.setCursor(0, 1);
  lcd.print(F("C : No  -  D : SI"));
  while (1) {
    char key = KeyPad.waitForKey();
    tone(TonePin, ToneBip, 30);
    if (key == 'd') {
      return true;
    }
    if (key == 'c') {
      return false;
    }
  }
}

byte KeyGetNumber() {
  char key = KeyPad.getKey();
  if (key == '1') {
    return 1;
  }
  if (key == '2') {
    return 2;
  }
  if (key == '3') {
    return 3;
  }
  if (key == '4') {
    return 4;
  }
  if (key == '5') {
    return 5;
  }
  if (key == '6') {
    return 6;
  }
  if (key == '7') {
    return 7;
  }
  if (key == '8') {
    return 8;
  }
  if (key == '9') {
    return 9;
  }
  if (key == '0') {
    return 0;
  }
  return 11;
}

void LCD_Welcome(){
  lcd.setCursor(0, 0);
  lcd.print(F("    SOFTAIR BOMB    "));
  lcd.setCursor(0, 1);
  lcd.print(F("  FIRMWARE REV 5.1  "));
  lcd.setCursor(0, 2);
  lcd.print(F("                    "));
  lcd.setCursor(0, 3);
  lcd.print(F("  ESBOLLATI  PRATO  "));
  delay(5000);
}

void LCD_CreateBar(){
  byte bar1[8] = {    B10000,    B10000,    B10000,    B10000,    B10000,    B10000,    B10000,    B10000,  };
  byte bar2[8] = {    B11000,    B11000,    B11000,    B11000,    B11000,    B11000,    B11000,    B11000,  };
  byte bar3[8] = {    B11100,    B11100,    B11100,    B11100,    B11100,    B11100,    B11100,    B11100,  };
  byte bar4[8] = {    B11110,    B11110,    B11110,    B11110,    B11110,    B11110,    B11110,    B11110,  };
  byte bar5[8] = {    B11111,    B11111,    B11111,    B11111,    B11111,    B11111,    B11111,    B11111,  };
  byte up[8]   = {    B00000,    B00100,    B01110,    B11111,    B11111,    B00000,    B00000,  };
  byte down[8] = {    B00000,    B00000,    B11111,    B11111,    B01110,    B00100,    B00000,  };
  lcd.createChar(0, bar1);
  lcd.createChar(1, bar2);
  lcd.createChar(2, bar3);
  lcd.createChar(3, bar4);
  lcd.createChar(4, bar5);
  lcd.createChar(5, up);
  lcd.createChar(6, down);
}

void LCD_Cls() {
  lcd.setCursor(0, 0);
  lcd.print(F("                    "));
  lcd.setCursor(0, 1);
  lcd.print(F("                    "));
  lcd.setCursor(0, 0);
}

void LCD_Clear(){
  //lcd.clear();
  lcd.setCursor(0, 0);
  lcd.print(F("                    "));
  lcd.setCursor(0, 1);
  lcd.print(F("                    "));
  lcd.setCursor(0, 0);
}

void LCD_Percentage(byte porcent) {
  int aDibujar = (8 * porcent) / 8;
  lcd.setCursor(0, 1);
  if (aDibujar < 5)
  {
    switch (aDibujar) {
      case 0:
        break;
      case 1:
        lcd.write((uint8_t)0);
        break;
      case 2:
        lcd.write(1);
        break;
      case 3:
        lcd.write(2);
        break;
      case 4:
        lcd.write(3);
        break;
    }
  }
  while (aDibujar >= 5) {
    if (aDibujar >= 5)
    {
      lcd.write(4);
      aDibujar -= 5;
    }
    if (aDibujar < 5)
    {
      switch (aDibujar) {
        case 0:
          break;
        case 1:
          lcd.write((uint8_t)0);
          break;
        case 2:
          lcd.write(1);
          break;
        case 3:
          lcd.write(2);
          break;
        case 4:
          lcd.write(3);
          break;
      }
    }
  }
}

void checkArrows(byte i, byte maxx ) {
  if (i == 0) {
    lcd.setCursor(19, 1);
    lcd.write(6);
  }
  if (i == maxx) {
    lcd.setCursor(19, 0);
    lcd.write(5);
  }
  if (i > 0 && i < maxx) {
    lcd.setCursor(19, 1);
    lcd.write(6);
    lcd.setCursor(19, 0);
    lcd.write(5);
  }
}

void MenuMain() {
  digitalWrite(GREENLED, LOW);
  digitalWrite(REDLED, LOW);
  digitalWrite(ALARM, LOW);
  LCD_Cls();
  int i = 0;
  int j = 100;
  int MaxMenu = 5;      // NUMBER OF VOICES ON MAIN MENU (-1)
  char var;
  delay(100);
  lcd.setCursor(0, 2);
  lcd.print(F("- MENU  PRINCIPALE -"));
  lcd.setCursor(0, 3);
  lcd.print(F("D=SELEZIONA - C=INFO"));
  while (1) {
    GAMETYPE = i;
    var = KeyPad.getKey();
    if (j != i) {
      tone(TonePin, ToneBip, 30);
      LCD_Cls();
      if(i==0) lcd.print(F("Piazza e Disarma   "));
      if(i==1) lcd.print(F("Sabotaggio         "));
      if(i==2) lcd.print(F("Dominazione        "));
      if(i==3) lcd.print(F("Cattura Bandiera   "));
      if(i==4) lcd.print(F("Cronometro Rientri "));
      if(i==5) lcd.print(F("Configurazione     "));
      checkArrows(i, MaxMenu);
      delay(250);
      j = i;
    }
    delay(50);
    if (var == 'a' && i > 0) {
      i--;
    }
    if (var == 'b' && i < MaxMenu) {
      i++;
    }
    if (var == 'c') {
      Help();
    }
    if (var == 'd') {
      tone(TonePin, ToneBip, 30);
      LCD_Cls();
      switch (i) {
        case 0:
          GAMETYPE = 1;
          GameConfig();
          SearchDestroy();
          break;
        case 1:
          GAMETYPE = 2;
          GameConfig();
          Sabotage();
          break;
        case 2:
          GAMETYPE = 3;
          GameConfig();
          Domination();
          break;
        case 3:
          GAMETYPE = 4;
          GameConfig();
          Capture();
          break;
        case 4:
          GAMETYPE = 5;
          GameConfig();
          Chrono();
          break;
        case 5:
          MenuConfig();
          break;
      }
    }
  }
}

void MenuConfig() {
  LCD_Cls();
  int i = 0;
  int j = 100;
  int MaxMenu = 6;      // NUMBER OF VOICES ON MAIN MENU -1
  char var;
  bool answer;
  delay(100);
  lcd.setCursor(0, 2);
  lcd.print(F("-  CONFIGURAZIONE  -"));
  lcd.setCursor(0, 3);
  lcd.print(F("D=SELEZIONA - C=MENU"));
  while (1) {
    var = KeyPad.getKey();
    if (j != i) {
      tone(TonePin, ToneBip, 30);
      LCD_Cls();
      if(i==0) lcd.print(F("Configura Gioco    "));
      if(i==1) lcd.print(F("Configura Audio    "));
      if(i==2) lcd.print(F("Test Allarme       "));
      if(i==3) lcd.print(F("Test Audio         "));
      if(i==4) lcd.print(F("Test Led           "));
      if(i==5) lcd.print(F("Salva Impostazioni "));
      if(i==6) lcd.print(F("Carica Impostazioni"));
      checkArrows(i, MaxMenu);
      delay(250);
      j = i;
    }
    if (var == 'a' && i > 0) {
      i--;
    }
    if (var == 'b' && i < MaxMenu) {
      i++;
    }
    if (var == 'c') {
      tone(TonePin, ToneBip, 30);
      LCD_Cls;
      MenuMain();
    }
    if (var == 'd') {
      tone(TonePin, ToneBip, 30);
      LCD_Cls();
      switch (i) {
        case 0:
          ConfigGame();
          j = 100;
          break;
        case 1:
          ConfigAudio();
          j = 100;
          break;
        case 2:
          TestAlarm();
          j = 100;
          break;
        case 3:
          TestBuzzer();
          j = 100;
          break;
        case 4:
          TestLed();
          j = 100;
          break;
        case 5:
          LCD_Cls();
          lcd.print(F("Salvo Impostazioni?"));
          answer = KeyYesNo();
          if (answer == true){
            SetConfig();
            SaveConfig();
          }
          j = 100;
          break;
        case 6:
          LCD_Cls();
          lcd.print(F("Carico Impostazioni?"));
          answer = KeyYesNo();
          if (answer == true){
            if(CheckConfig()){LoadConfig();}
          }
          j = 100;
          break;
      }
    }
  }
}

void ConfigGame(){
  lcd.setCursor(0, 2);
  lcd.print(F("-   CONFIG. GIOCO  -"));
  lcd.setCursor(0, 3);
  lcd.print(F("D=SELEZIONA - C=DEL "));
  lcd.setCursor(0, 0);
  GAMEHOURS = MenuAskNumber2(1,"HH","--",DigitRestInt(GAMEHOURS,0,2),DigitRestInt(GAMEHOURS,1,2));
  GAMEMINUTES = MenuAskNumber2(1,"minuti","--",DigitRestInt(GAMEMINUTES,0,2),DigitRestInt(GAMEMINUTES,1,2));
  BOMBMINUTES = MenuAskNumber2(2,"minuti","--",DigitRestInt(BOMBMINUTES,0,2),DigitRestInt(BOMBMINUTES,1,2));
  ACTIVATESECONDS = MenuAskNumber2(3,"secondi","--",DigitRestInt(ACTIVATESECONDS,0,2),DigitRestInt(ACTIVATESECONDS,1,2));
  CAPTURESECONDS = MenuAskNumber2(4,"secondi","--",DigitRestInt(CAPTURESECONDS,0,2),DigitRestInt(CAPTURESECONDS,1,2));
  CATCHPOINTMINUTES = MenuAskNumber2(5,"minuti","--",DigitRestInt(CATCHPOINTMINUTES,0,2),DigitRestInt(CATCHPOINTMINUTES,1,2));
  SQLIFES = MenuAskNumber2(6,"vite","--",DigitRestInt(SQLIFES,0,2),DigitRestInt(SQLIFES,1,2));
  MenuConfig();
}

void ConfigAudio(){
  lcd.setCursor(0, 2);
  lcd.print(F("-   CONFIG. AUDIO  -"));
  lcd.setCursor(0, 3);
  lcd.print(F("D=SELEZIONA - C=DEL "));
  lcd.setCursor(0, 0);
  ToneAlarm1 = MenuAskNumber4(1,"Hz","0000",DigitRestInt(ToneAlarm1,0,4),DigitRestInt(ToneAlarm1,1,4),DigitRestInt(ToneAlarm1,2,4),DigitRestInt(ToneAlarm1,3,4));tone(TonePin, ToneAlarm1, 500);
  ToneAlarm2 = MenuAskNumber4(2,"Hz","0000",DigitRestInt(ToneAlarm2,0,4),DigitRestInt(ToneAlarm2,1,4),DigitRestInt(ToneAlarm2,2,4),DigitRestInt(ToneAlarm2,3,4));tone(TonePin, ToneAlarm2, 500);
  ToneArming = MenuAskNumber4(3,"Hz","0000",DigitRestInt(ToneArming,0,4),DigitRestInt(ToneArming,1,4),DigitRestInt(ToneArming,2,4),DigitRestInt(ToneArming,3,4));tone(TonePin, ToneArming, 500);
  ToneError  = MenuAskNumber4(4,"Hz","0000",DigitRestInt(ToneError,0,4),DigitRestInt(ToneError,1,4),DigitRestInt(ToneError,2,4),DigitRestInt(ToneError,3,4));tone(TonePin, ToneError, 500);
  ToneBip    = MenuAskNumber4(5,"Hz","0000",DigitRestInt(ToneBip,0,4),DigitRestInt(ToneBip,1,4),DigitRestInt(ToneBip,2,4),DigitRestInt(ToneBip,3,4));tone(TonePin, ToneBip, 500);
  MenuConfig();
}

void GameConfig() {
  lcd.setCursor(0, 2);
  lcd.print(F("-   CONFIG. GIOCO  -"));
  lcd.setCursor(0, 3);
  lcd.print(F("D=SELEZIONA - C=DEL "));
  lcd.setCursor(0, 0);
  if ( GAMETYPE == 1 || GAMETYPE == 2 || GAMETYPE == 3 || GAMETYPE == 4 || GAMETYPE == 5) {
    GAMEMINUTES = MenuAskTime4(1,"hh:mm","--:--",DigitRestInt(GAMEHOURS,0,2),DigitRestInt(GAMEHOURS,1,2),DigitRestInt(GAMEMINUTES,0,2),DigitRestInt(GAMEMINUTES,1,2));
  }
  if ( GAMETYPE == 1 || GAMETYPE == 2) {
    BOMBMINUTES = MenuAskTime2(1,"minuti","--",DigitRestInt(BOMBMINUTES,0,2),DigitRestInt(BOMBMINUTES,1,2));
  }

  if ( GAMETYPE == 1 || GAMETYPE == 2) {
    ACTIVATESECONDS = MenuAskTime2(2,"secondi","--",DigitRestInt(ACTIVATESECONDS,0,2),DigitRestInt(ACTIVATESECONDS,1,2));
  }
  if ( GAMETYPE == 3 || GAMETYPE == 4 ) {
    ACTIVATESECONDS = MenuAskTime2(3,"secondi","--",DigitRestInt(ACTIVATESECONDS,0,2),DigitRestInt(ACTIVATESECONDS,1,2));
  }
  if ( GAMETYPE == 5) {
    BOMBMINUTES = MenuAskTime2(4,"minuti","--",DigitRestInt(BOMBMINUTES,0,2),DigitRestInt(BOMBMINUTES,1,2));
    SQLIFES =     MenuAskTime2(5,"vite","--",DigitRestInt(SQLIFES,0,2),DigitRestInt(SQLIFES,1,2));
  }
  if ( GAMETYPE == 1 || GAMETYPE == 2 || GAMETYPE == 3 || GAMETYPE == 4 || GAMETYPE == 5) {
    LCD_Cls();
    lcd.print(F("Abilta Sirena?"));
    ALARMACTIVE = KeyYesNo();
  }
  if ( GAMETYPE == 1 || GAMETYPE == 2 || GAMETYPE == 3 || GAMETYPE == 4) {
    LCD_Cls();
    lcd.print(F("Abilita Taglio Cavi?"));
    SMARTCARDACTIVE = KeyYesNo();
  }
  if (( GAMETYPE == 1 || GAMETYPE == 2) && SMARTCARDACTIVE == false) {
    LCD_Cls();
    lcd.print(F("Abilita Codice?"));
    PASSWORDACTIVE = KeyYesNo();
    if(PASSWORDACTIVE == true){
      SetPassword();
    }
  }
}

void Sabotage(){
  StartGameCount();
  LCD_Cls();
  digitalWrite(REDLED, LOW);
  digitalWrite(GREENLED, LOW);
  lcd.setCursor(0, 2);
  lcd.print("--------------------");
  lcd.setCursor(0, 3);
  lcd.print("     SABOTAGGIO     ");
  minutos = GAMEMINUTES - 1;
  iTime=0;
  PLAYING = false;
  SabotagePlay();
}

void SabotagePlay(){
  unsigned long timeCalcVar;
  unsigned long aTime;
  if(PLAYING = true){
    iTime = millis();
  }
  while (1) {
    timeCalcVar = (millis() - iTime) % 1000;
    if (timeCalcVar >= 0 && timeCalcVar <= 50)
    {
      digitalWrite(GREENLED, HIGH);
    }
    if (timeCalcVar >= 90 && timeCalcVar <= 130)
    {
      digitalWrite(GREENLED, LOW);
    }
    lcd.setCursor(0, 0);
    lcd.print("   TEMPO DI GIOCO   ");
    aTime = millis() - iTime;
    lcd.setCursor(5, 1);
    PrintTime(minutos, aTime);
    if (minutos - aTime / 60000 == 0 && 59 - ((aTime / 1000) % 60) == 0)
    {
      EndDefenderWin();
    }
    if (KeyPad.getKey() == 'd' && PASSWORDACTIVE == true && SMARTCARDACTIVE == false) {
      bool armings = ArmPassword("ARMING BOMB");
      if (armings == true) {
        PlayForDefuseNow();
      }else{ALARM_OFF();}
    }
    if (digitalRead(SMARTCARD) == HIGH && SMARTCARDACTIVE == true) {
      bool armings = ArmSmartCard("ARMING BOMB");
      if (armings == true) {
        PlayForDefuseNow();
      }else{ALARM_OFF();}
    }
    if (ARMING == true && PASSWORDACTIVE == false && SMARTCARDACTIVE == false) {
      bool armings = ArmKeyHold("ARMING BOMB");
      if (armings == true) {
        DEFUSE = false;
        ARMING = false;
        PlayForDefuseNow();
      }else{ALARM_OFF();}
    }
  }
}

void PlayForDefuseNow(){
  LCD_Cls();
  digitalWrite(REDLED, HIGH);
  digitalWrite(GREENLED, HIGH);
  int minutos = BOMBMINUTES - 1;
  unsigned long iTime = millis();
  unsigned long timeCalcVar;
  unsigned long aTime;
  int TonoLong = 50;
  PLAYING=true;

  while (1) {
    timeCalcVar = (millis() - iTime) % 1000;
    if (timeCalcVar >= 0 && timeCalcVar <= 60)
    {
      digitalWrite(REDLED, HIGH);
      tone(ToneArming, ToneBip, TonoLong);
      ALARM_ON();
    } else {
      ALARM_OFF();
    }
    if (timeCalcVar >= 180 && timeCalcVar <= 220)
    {
      digitalWrite(REDLED, LOW);
      tone(ToneArming, ToneBip, TonoLong);
    }
    aTime = millis() - iTime;
    timeCalcVar = (millis() - iTime) % 1000;
    if (timeCalcVar >= 245 && timeCalcVar <= 255 && minutos - aTime / 60000 < 2 )tone(ToneArming, ToneBip, TonoLong);
    if (timeCalcVar >= 495 && timeCalcVar <= 510 && minutos - aTime / 60000 < 4 )tone(ToneArming, ToneBip, TonoLong);
    if (timeCalcVar >= 745 && timeCalcVar <= 760 && minutos - aTime / 60000 < 2 )tone(ToneArming, ToneBip, TonoLong);
    if ( minutos - aTime / 60000 == 0 && 59 - ((aTime / 1000) % 60) < 10)TonoLong = 300;
    lcd.setCursor(2, 0);
    lcd.print("LA BOMBA ESPLODE IN");
    lcd.setCursor(5, 1);
    PrintTime(minutos, aTime);
    if (minutos - aTime / 60000 == 0 && 59 - ((aTime / 1000) % 60) == 0)
    {
      EndAttackerWin();
    }
    if (KeyPad.getKey() == 'd' && PASSWORDACTIVE == true && SMARTCARDACTIVE == false) {
      bool disarmings = ArmPassword("DISARMING BOMB");
      if (disarmings == true) {
        SabotagePlay();
      }else{ALARM_OFF();}
    }
    if (digitalRead(SMARTCARD) == HIGH && SMARTCARDACTIVE == true) {
      bool disarmings = ArmSmartCard("DISARMING BOMB");
      if (disarmings == true) {
        SabotagePlay();
      }else{ALARM_OFF();}
    }
    if (DEFUSE == true && PASSWORDACTIVE == false && SMARTCARDACTIVE == false) {
      bool disarmings = DefuseKeyHold("DISARMING BOMB");
      if (disarmings == true) {
        SabotagePlay();
      }else{ALARM_OFF();}
    }
  }
}

void SearchDestroy(){
  StartGameCount();
  LCD_Cls();
  digitalWrite(REDLED, LOW);
  digitalWrite(GREENLED, LOW);
  lcd.setCursor(0, 2);
  lcd.print("--------------------");
  lcd.setCursor(0, 3);
  lcd.print("  PIAZZA E DISARMA  ");
  minutos = GAMEMINUTES - 1;
  iTime=0;
  PLAYING = false;
  PlayForArm();
}

void PlayForArm(){
  unsigned long timeCalcVar;
  unsigned long aTime;
  if(PLAYING = true){
    iTime = millis();
  }
  while (1) {
    timeCalcVar = (millis() - iTime) % 1000;
    if (timeCalcVar >= 0 && timeCalcVar <= 50)
    {
      digitalWrite(GREENLED, HIGH);
    }
    if (timeCalcVar >= 90 && timeCalcVar <= 130)
    {
      digitalWrite(GREENLED, LOW);
    }
    lcd.setCursor(0, 0);
    lcd.print("   TEMPO DI GIOCO   ");
    aTime = millis() - iTime;
    lcd.setCursor(5, 1);
    PrintTime(minutos, aTime);
    if (minutos - aTime / 60000 == 0 && 59 - ((aTime / 1000) % 60) == 0)
    {
      EndDefenderWin();
    }
    if (KeyPad.getKey() == 'd' && PASSWORDACTIVE == true && SMARTCARDACTIVE == false) {
      bool armings = ArmPassword("ARMING BOMB");
      if (armings == true) {
        PlayForDefuse();
      }else{ALARM_OFF();}
    }
    if (digitalRead(SMARTCARD) == HIGH && SMARTCARDACTIVE == true) {
      bool armings = ArmSmartCard("ARMING BOMB");
      if (armings == true) {
        PlayForDefuse();
      }else{ALARM_OFF();}
    }
    if (ARMING == true && PASSWORDACTIVE == false && SMARTCARDACTIVE == false) {
      bool armings = ArmKeyHold("ARMING BOMB");
      if (armings == true) {
        PlayForDefuse();
      }else{ALARM_OFF();}
    }
  }
}

void PlayForDefuse(){
  LCD_Cls();
  digitalWrite(REDLED, HIGH);
  digitalWrite(GREENLED, HIGH);
  int minutos = BOMBMINUTES - 1;
  iTime = millis();
  unsigned long timeCalcVar;
  unsigned long aTime;
  int TonoLong = 50;

  while (1) {
    timeCalcVar = (millis() - iTime) % 1000;
    if (timeCalcVar >= 0 && timeCalcVar <= 60)
    {
      digitalWrite(REDLED, HIGH);
      tone(ToneArming, ToneBip, TonoLong);
      ALARM_ON();
    } else {
      ALARM_OFF();
    }
    if (timeCalcVar >= 180 && timeCalcVar <= 220)
    {
      digitalWrite(REDLED, LOW);
      tone(ToneArming, ToneBip, TonoLong);
    }
    aTime = millis() - iTime;
    timeCalcVar = (millis() - iTime) % 1000;
    if (timeCalcVar >= 245 && timeCalcVar <= 255 && minutos - aTime / 60000 < 2 )tone(ToneArming, ToneBip, TonoLong);
    if (timeCalcVar >= 495 && timeCalcVar <= 510 && minutos - aTime / 60000 < 4 )tone(ToneArming, ToneBip, TonoLong);
    if (timeCalcVar >= 745 && timeCalcVar <= 760 && minutos - aTime / 60000 < 2 )tone(ToneArming, ToneBip, TonoLong);
    if ( minutos - aTime / 60000 == 0 && 59 - ((aTime / 1000) % 60) < 10)TonoLong = 300;
    lcd.setCursor(2, 0);
    lcd.print("LA BOMBA ESPLODE IN");
    lcd.setCursor(5, 1);
    PrintTime(minutos, aTime);
    if (minutos - aTime / 60000 == 0 && 59 - ((aTime / 1000) % 60) == 0)
    {
      EndAttackerWin();
    }
    if (KeyPad.getKey() == 'd' && PASSWORDACTIVE == true && SMARTCARDACTIVE == false) {
      bool disarmings = ArmPassword("DISARMING BOMB");
      if (disarmings == true) {
        EndDefenderWin();
      }else{ALARM_OFF();}
    }
    if (digitalRead(SMARTCARD) == HIGH && SMARTCARDACTIVE == true) {
      bool disarmings = ArmSmartCard("DISARMING BOMB");
      if (disarmings == true) {
        EndDefenderWin();
      }else{ALARM_OFF();}
    }
    if (DEFUSE == true && PASSWORDACTIVE == false && SMARTCARDACTIVE == false) {
      bool disarmings = DefuseKeyHold("DISARMING BOMB");
      if (disarmings == true) {
        EndDefenderWin();
      }else{ALARM_OFF();}
    }
  }
}

void TestAlarm() {
  LCD_Cls();
  lcd.print(F("TEST SIRENA"));
  digitalWrite(ALARM, HIGH);
  PressKeyToStop();
  digitalWrite(ALARM, LOW);
  delay(500);
}

void TestBuzzer() {
  LCD_Cls(); lcd.print(F("TEST Tone ALARM1"));
  tone(TonePin, ToneAlarm1, 500);
  PressKeyToStop();
  LCD_Cls(); lcd.print(F("TEST Tone ALARM2"));
  tone(TonePin, ToneAlarm2, 500);
  PressKeyToStop();
  LCD_Cls(); lcd.print(F("TEST Tone ARM   "));
  tone(TonePin, ToneArming, 500);
  PressKeyToStop();
  LCD_Cls(); lcd.print(F("TEST Tone ERROR "));
  tone(TonePin, ToneError, 500);
  PressKeyToStop();
  LCD_Cls(); lcd.print(F("TEST Tone BIP   "));
  tone(TonePin, ToneBip, 500);
  PressKeyToStop();
  delay(200);
}

void TestLed(){
  LCD_Cls(); lcd.print(F("TEST LED VERDE"));
  digitalWrite(GREENLED, HIGH);  digitalWrite(GREENLED, LOW);
  delay(200);
  LCD_Cls(); lcd.print(F("TEST LED ROSSO"));
  digitalWrite(REDLED, HIGH);  digitalWrite(REDLED, LOW);
  delay(200);
  LCD_Cls(); lcd.print(F("TEST LED BOMBA"));
  digitalWrite(BOOMLED, HIGH);  digitalWrite(BOOMLED, LOW);
  delay(200);
}


int DigitRestInt(int Numbers, int Poss, int Len) {
  String Nums = String(Numbers);
  while (Nums.length() < Len){
    Nums = "0" + Nums;
  }
  String Chrz = Nums.substring(Poss, Poss + 1);
  int Ret = Chrz.toInt();
  return (Ret);
}

bool ArmKeyHold(char* txt) {
  digitalWrite(GREENLED, LOW);
  LCD_Cls();
  lcd.setCursor(2, 0);
  lcd.print(txt);
  lcd.setCursor(0, 1);
  unsigned int percent = 0;
  unsigned long xTime = millis();
  unsigned long timeCalcVar;
  while (ARMING == true) {
    KeyPad.getKey();
    timeCalcVar = (millis() - xTime) % 1000;
    if ( timeCalcVar >= 0 && timeCalcVar <= 50)
    {
      digitalWrite(REDLED, HIGH);
      tone(TonePin, ToneAlarm1, 200);
      ALARM_OFF();
    } else {
      ALARM_ON();
    }
    if (timeCalcVar >= 470 && timeCalcVar <= 520)
    {
      tone(TonePin, ToneAlarm2, 200);
      digitalWrite(REDLED, LOW);
    }
    unsigned long seconds = millis() - xTime;
    percent = (seconds) / (ACTIVATESECONDS * 10);
    LCD_Percentage(percent);
    if (percent >= 100)
    {
      digitalWrite(REDLED, HIGH);
      digitalWrite(GREENLED, HIGH);
      digitalWrite(BTNLED, HIGH);
      return true;
      break;
    }
  }
  LCD_Cls();
      digitalWrite(REDLED, LOW);
      digitalWrite(GREENLED, LOW);
      digitalWrite(BTNLED, LOW);
  return false;
}

bool DefuseKeyHold(char* txt) {
  digitalWrite(GREENLED, LOW);
  LCD_Cls();
  lcd.setCursor(2, 0);
  lcd.print(txt);
  lcd.setCursor(0, 1);
  unsigned int percent = 0;
  unsigned long xTime = millis();
  unsigned long timeCalcVar;
  while (DEFUSE == true) {
    KeyPad.getKey();
    timeCalcVar = (millis() - xTime) % 1000;
    if ( timeCalcVar >= 0 && timeCalcVar <= 40)
    {
      digitalWrite(REDLED, HIGH);
      tone(TonePin, ToneAlarm1, 200);
      ALARM_ON();
    }
    if (timeCalcVar >= 480 && timeCalcVar <= 520)
    {
      tone(TonePin, ToneAlarm2, 200);
      digitalWrite(REDLED, LOW);
      ALARM_OFF();
    }
    unsigned long seconds = millis() - xTime;
    percent = (seconds) / (ACTIVATESECONDS * 10);
    LCD_Percentage(percent);
    if (percent >= 100)
    {
      digitalWrite(REDLED, LOW);
      digitalWrite(GREENLED, LOW);
      digitalWrite(BTNLED, LOW);
      return true;
      break;
    }
  }
  LCD_Cls();
      digitalWrite(REDLED, HIGH);
      digitalWrite(GREENLED, HIGH);
      digitalWrite(BTNLED, HIGH);
  return false;
}

bool ArmPassword(char* txt) {
  LCD_Clear();
  digitalWrite(GREENLED, LOW);
  digitalWrite(REDLED, HIGH);
  lcd.setCursor(3, 0);
  lcd.print(txt);
  delay(1000);
  LCD_Cls();
  lcd.setCursor(0, 0);
  AskPassword("Inserisci Password:");
  for (int i = 0; i < 4; i++) {
    enteredText[i] = temptext[i];
  }
  if (CheckPassword()) {
      digitalWrite(REDLED, HIGH);
      digitalWrite(GREENLED, HIGH);
      digitalWrite(BTNLED, LOW);
    return true;
  } else {
    LCD_Cls();
    lcd.setCursor(0, 0);
    lcd.print("ERRORE PASSWORD !!!!");
    tone(TonePin, ToneError, 30);
    delay(500);
      digitalWrite(REDLED, LOW);
      digitalWrite(GREENLED, LOW);
      digitalWrite(BTNLED, LOW);
    LCD_Cls();
    return false;
  }
}

bool ArmSmartCard(char* txt) {
  digitalWrite(GREENLED, LOW);
  lcd.clear();
  lcd.setCursor(2, 0);
  lcd.print(txt);
  lcd.setCursor(0, 1);
  unsigned int percent = 0;
  unsigned long xTime = millis();
  unsigned long timeCalcVar;
  while (digitalRead(SMARTCARD) == HIGH) {
    timeCalcVar = (millis() - xTime) % 1000;
    if ( timeCalcVar >= 0 && timeCalcVar <= 40)
    {
      digitalWrite(REDLED, HIGH);
      tone(TonePin, ToneAlarm1, 200);
      ALARM_ON();
    }
    if (timeCalcVar >= 480 && timeCalcVar <= 520)
    {
      tone(TonePin, ToneAlarm2, 200);
      digitalWrite(REDLED, LOW);
      ALARM_OFF();
    }
    unsigned long seconds = millis() - xTime;
    percent = (seconds) / (ACTIVATESECONDS * 10);
    LCD_Percentage(percent);
    if (percent >= 100)
    {
      digitalWrite(REDLED, HIGH);
      digitalWrite(GREENLED, HIGH);
      digitalWrite(BTNLED, LOW);
      return true;
      break;
    }
  }
  LCD_Cls();
      digitalWrite(REDLED, LOW);
      digitalWrite(GREENLED, LOW);
      digitalWrite(BTNLED, LOW);
  return false;
}

void SetPassword() {
ReType:
  LCD_Cls();
  AskPassword("Inserisci Password:");
  for (int i = 0; i < 4; i++) {
    password[i] = temptext[i];
  }
  AskPassword("Ripeti Password:");
  for (int i = 0; i < 4; i++) {
    enteredText[i] = temptext[i];
  }
  if (CheckPassword()) {
    LCD_Cls();
    lcd.setCursor(0, 0);
    lcd.print(F("Password Salvata!"));
    delay(2000);
  } else {
    LCD_Cls();
    lcd.setCursor(0, 0);
    lcd.print(F("ERRORE NON UGUALE"));
    tone(TonePin, ToneError, 30);
    delay(2000);
    goto ReType;
  }
}

boolean CheckPassword() {
  for (int i = 0; i < 4; i++) {
    if (enteredText[i] != password[i])return false;
  }
  return true;
}

void AskPassword(char* quest) {
  LCD_Clear();
  lcd.setCursor(0, 0);
  lcd.print(quest);
  lcd.setCursor(8, 1);
  lcd.print("----");
  lcd.cursor();
  lcd.blink();
  lcd.setCursor(8, 1);
  for (int i = 0; i < 4; i++) {
    byte number = 11;
    while (number == 11) {
      number = KeyGetNumber();
    }
    lcd.setCursor((i+8), 1);
    lcd.print("*");
    temptext[i] =  number;
    tone(TonePin, ToneBip, 30);
  }
  lcd.noCursor();
  lcd.noBlink();
}

int MenuAskTime2(int quest, char* type, char* std, int t1, int t2) {
ReAsk:
  LCD_Cls();
  lcd.setCursor(0, 0);
  if (quest == 1) {lcd.print(F("Tempo Detonazione:"));}
  if (quest == 2) {lcd.print(F("Tempo per ARM/DIS:"));}
  if (quest == 3) {lcd.print(F("Tempo Cattura Punto:"));}
  if (quest == 4) {lcd.print(F("Tempo Rientro:"));}
  if (quest == 5) {lcd.print(F("Numero Vite Squadra"));}
  lcd.setCursor(3, 1);
  lcd.print(type);
  lcd.setCursor(0, 1);
  lcd.print(std);
  lcd.setCursor(0, 1);
  lcd.print(t1);
  lcd.print(t2);
  lcd.cursor();
  lcd.blink();
  lcd.setCursor(0, 1);
  for (int i = 0; i < 2; i++) {
    byte number = 99;
    while (number == 99) {
      number = KeyGetNumber();
      if (number == 11) {
        time[0] = t1;
        time[1] = t2;
        goto EndProg;
        break;
      }
      if (number == 10) {
        goto ReAsk;
        break;
      }
    }
    tone(13, 2400, 30);
    time[i] = number;
    lcd.print(number);
    delay(250);
  }
EndProg:
  lcd.noCursor();
  lcd.noBlink();
  if (KeyConfirm() == false) {
    goto ReAsk;
  }
  return ((time[0] * 10) + (time[1]));
}

int MenuAskTime4(int quest, char* type, char* std, int t1, int t2, int t3, int t4) {
ReAsk:
  LCD_Cls();
  lcd.setCursor(0, 0);
  if (quest == 1) {lcd.print(F("Tempo Max. di Gioco:"));}
  lcd.setCursor(6, 1);
  lcd.print(type);
  lcd.setCursor(0, 1);
  lcd.print(std);
  lcd.setCursor(0, 1);
  lcd.print(t1);
  lcd.print(t2);
  lcd.print(":");
  lcd.print(t3);
  lcd.print(t4);
  lcd.cursor();
  lcd.blink();
  lcd.setCursor(0, 1);
  for (int i = 0; i < 4; i++) {
    if (i == 2) {
      lcd.print(":");
    }
    byte number = 99;
    while (number == 99) {
      number = KeyGetNumber();
      if (number == 11) {
        time[0] = t1;
        time[1] = t2;
        time[2] = t3;
        time[3] = t4;
        goto EndProg;
        break;
      }
      if (number == 10) {
        goto ReAsk;
        break;
      }
    }
    tone(13, 2400, 30);
    time[i] = number;
    lcd.print(number);
    delay(250);
  }
EndProg:
  lcd.noCursor();
  lcd.noBlink();
  if (KeyConfirm() == false) {
    goto ReAsk;
  }
  return ((time[0] * 600) + (time[1] * 60) + (time[2] * 10) + (time[3]));
}

int MenuAskNumber4(int quest, char* type, char* std, int t1, int t2, int t3, int t4) {
ReAsk:
  LCD_Cls();
  lcd.setCursor(0, 0);
  if (quest == 1) {lcd.print(F("Tone ALARM 1:"));}
  if (quest == 2) {lcd.print(F("Tone ALARM 2:"));}
  if (quest == 3) {lcd.print(F("Tone ARMING:"));}
  if (quest == 4) {lcd.print(F("Tone ERROR:"));}
  if (quest == 5) {lcd.print(F("Tone BIP:"));}
  lcd.setCursor(6, 1);
  lcd.print(type);
  lcd.setCursor(0, 1);
  lcd.print(std);
  lcd.setCursor(0, 1);
  lcd.print(t1);
  lcd.print(t2);
  lcd.print(t3);
  lcd.print(t4);
  lcd.cursor();
  lcd.blink();
  lcd.setCursor(0, 1);
  for (int i = 0; i < 4; i++) {
    byte number = 99;
    while (number == 99) {
      number = KeyGetNumber();
      if (number == 11) {
        time[0] = t1;
        time[1] = t2;
        time[2] = t3;
        time[3] = t4;
        goto EndProg;
        break;
      }
      if (number == 10) {
        goto ReAsk;
        break;
      }
    }
    tone(13, 2400, 30);
    time[i] = number;
    lcd.print(number);
    delay(250);
  }
EndProg:
  lcd.noCursor();
  lcd.noBlink();
  if (KeyConfirm() == false) {
    goto ReAsk;
  }
  return ((time[0] * 1000) + (time[1] * 100) + (time[2] * 10) + (time[3]));
}

int MenuAskNumber2(int quest, char* type, char* std, int t1, int t2) {
ReAsk:
  LCD_Cls();
  lcd.setCursor(0, 0);
  if (quest == 1) {lcd.print(F("Max Tempo Gioco:"));}
  if (quest == 2) {lcd.print(F("Tempo Detonazione:"));}
  if (quest == 3) {lcd.print(F("Tempo ARM/DIS:"));}
  if (quest == 4) {lcd.print(F("Tempo Cattura:"));}
  if (quest == 5) {lcd.print(F("Tempo Conquista:"));}
  if (quest == 6) {lcd.print(F("Numero di Vite:"));}
  lcd.setCursor(6, 1);
  lcd.print(type);
  lcd.setCursor(0, 1);
  lcd.print(std);
  lcd.setCursor(0, 1);
  lcd.print(t1);
  lcd.print(t2);
  lcd.cursor();
  lcd.blink();
  lcd.setCursor(0, 1);
  for (int i = 0; i < 2; i++) {
    byte number = 99;
    while (number == 99) {
      number = KeyGetNumber();
      if (number == 11) {
        time[0] = t1;
        time[1] = t2;
        goto EndProg;
        break;
      }
      if (number == 10) {
        goto ReAsk;
        break;
      }
    }
    tone(13, 2400, 30);
    time[i] = number;
    lcd.print(number);
    delay(250);
  }
EndProg:
  lcd.noCursor();
  lcd.noBlink();
  if (KeyConfirm() == false) {
    goto ReAsk;
  }
  return ((time[0] * 10) + (time[1]));
}

void PlayAgain() {
  LCD_Cls();
  PLAYING = false;
  lcd.print(F(" Giocare Ancora? "));
  lcd.setCursor(0, 1);
  lcd.print(F("C : No  -  D : SI"));
  while (1)
  {
    char key = KeyPad.waitForKey();
    if (key == 'd' ) {
      tone(TonePin, ToneBip, 30);
      switch (GAMETYPE) {
        case 0:
          SearchDestroy();
          break;
        case 1:
          Sabotage();
          break;
        case 2:
          Domination();
          break;
        case 3:
          Capture();
          break;
      }
    }
    if (key == 'c' ) {
      tone(TonePin, ToneBip, 30);
      Software_Reboot();
      break;
    }
  }
}

void StartGameCount() {
  LCD_Cls();
  lcd.setCursor(0, 0);
  lcd.print(F("PRONTO PER INIZIARE!"));
  lcd.setCursor(0, 1);
  lcd.print(F("                    "));
  lcd.setCursor(0, 2);
  lcd.print(F("                    "));
  lcd.setCursor(0, 3);
  lcd.print(F(" Premi un Pulsante! "));
  PressAKey();
  LCD_Cls();
  lcd.setCursor(0, 1);
  lcd.print(F(" ATTENDI 10 SECONDI "));
  for (int i = 9; i > 0 ; i--) {
    lcd.setCursor(9, 2);
    tone(TonePin, ToneBip, 30);
    lcd.print(i);
    delay(1000);
  }
  PLAYING = true;
  LCD_Cls();
}

void PrintTime(unsigned long minutos, unsigned long aTiempo) {
  unsigned long sectoprint;
  sectoprint = (minutos*60 - aTiempo/600);
  char str[12];
  long h = sectoprint / 3600;
  sectoprint = sectoprint % 3600;
  int m = sectoprint / 60;
  int s = sectoprint % 60;
  sprintf(str, "%04ld:%02d:%02d", h, m, s);
  lcd.print(str);
}

void EndNoWin() {
  LCD_Cls();
  lcd.print(F("  -- GAME  OVER --"));
  lcd.setCursor(0, 1);
  lcd.print(F("  TEMPO ESAURITO  "));
  for (int i = 1; i < 11; i++) {
    tone(TonePin, ToneBip, 30);
    delay(100);
  }
  noTone(TonePin);
  ALARM_ON();
  PressAKey();
  ALARM_OFF();
  PlayAgain();
}

void EndAttackerWin() {
  LCD_Cls();
  lcd.print(F("  -- GAME  OVER --"));
  lcd.setCursor(0, 1);
  lcd.print(F("VINCONO ATTACCANTI"));
  for (int i = 1; i < 11; i++) {
    tone(TonePin, ToneBip, 30);
    delay(100);
  }
  noTone(TonePin);
  ALARM_ON();
  PressAKey();
  ALARM_OFF();
  PlayAgain();
}

void EndDefenderWin() {
  LCD_Cls();
  lcd.print(F("  -- GAME  OVER --"));
  lcd.setCursor(0, 1);
  lcd.print(F("VINCONO DIFENSORI "));
  for (int i = 1; i < 11; i++) {
    tone(TonePin, ToneError, 30);
    delay(100);
  }
  noTone(TonePin);
  ALARM_ON();
  PressAKey();
  ALARM_OFF();
  PlayAgain();
}

void ALARM_ON() {
  if (ALARMACTIVE) {
    digitalWrite(ALARM, HIGH);
  }
}

void ALARM_OFF() {
  if (ALARMACTIVE) {
    digitalWrite(ALARM, LOW);
  }
}

void Software_Reboot(){
  wdt_enable(WDTO_15MS);
  while(1)
  {
  }
}
